# Fritzing sketch p1a-parkingsensor (saved by Fritzing 0.9.1b)
breadboards: 1

parts:
  Part1 = Arduino Mega 2560 (Rev3)
  LED4 = LED - 3mm [color="Green (555nm)" package="3 mm [THT]"]
  R1 = Resistor [package="2010 [SMD]"]
  J1 = Piezo Speaker
  Onderdeel1 = SRF05 Ultrasonic Rangefinder

nets:
  N1: Part1.A10, Onderdeel1.VCC
  N2: Part1.A11, Onderdeel1.Trig
  N3: Part1.A12, Onderdeel1.Echo
  N4: Part1.A13, Onderdeel1.GND
  N5: Part1.GND, R1.Pin_0, J1.pin1
  N6: Part1.D8_PWM, J1.pin2
  N7: Part1.D2_PWM, LED4.anode
  N8: LED4.cathode, R1.Pin_1
